// Logisim project 8_bit_numbers.circ as structural Verilog: 3 circuits, main circuit main
module main (
  input  A0,
  input  B0,
  input  A1,
  input  B1,
  input  A2,
  input  B2,
  input  A3,
  input  B3,
  input  A4,
  input  B4,
  input  A5,
  input  B5,
  input  A6,
  input  B6,
  input  A7,
  input  B7,
  output S0,
  output S1,
  output S2,
  output S3,
  output S4,
  output S5,
  output S6,
  output S7,
  output S8
);

  wire full_adder_1_carryout, full_adder_3_carryout, full_adder_4_carryout, full_adder_5_carryout,
       full_adder_6_carryout, full_adder_7_carryout, half_adder_1_caryout;

  full_adder full_adder_1 (.caryin(full_adder_7_carryout), .a(A6), .b(B6), .sum(S6), .carryout(full_adder_1_carryout));
  full_adder full_adder_2 (.caryin(full_adder_1_carryout), .a(A7), .b(B7), .sum(S7), .carryout(S8));
  full_adder full_adder_3 (.caryin(half_adder_1_caryout), .a(A1), .b(B1), .sum(S1), .carryout(full_adder_3_carryout));
  full_adder full_adder_4 (.caryin(full_adder_3_carryout), .a(A2), .b(B2), .sum(S2), .carryout(full_adder_4_carryout));
  full_adder full_adder_5 (.caryin(full_adder_4_carryout), .a(A3), .b(B3), .sum(S3), .carryout(full_adder_5_carryout));
  full_adder full_adder_6 (.caryin(full_adder_5_carryout), .a(A4), .b(B4), .sum(S4), .carryout(full_adder_6_carryout));
  full_adder full_adder_7 (.caryin(full_adder_6_carryout), .a(A5), .b(B5), .sum(S5), .carryout(full_adder_7_carryout));
  half_adder half_adder_1 (.a(B0), .b(A0), .sum(S0), .caryout(half_adder_1_caryout));
endmodule

module half_adder (
  input  a,
  input  b,
  output sum,
  output caryout
);

  xor xor_1 (sum, a, b);
  and and_1 (caryout, a, b);
endmodule

module full_adder (
  input  caryin,
  input  a,
  input  b,
  output sum,
  output carryout
);

  wire and_1_out, and_2_out, xor_1_out;

  and and_1 (and_1_out, a, b);
  xor xor_1 (xor_1_out, a, b);
  xor xor_2 (sum, caryin, xor_1_out);
  and and_2 (and_2_out, caryin, xor_1_out);
  or or_1 (carryout, and_2_out, and_1_out);
endmodule
